// Digital circuit register-file.dig as structural Verilog
module register_file (
  input  [4:0] ReadReg1,
  input  [4:0] ReadReg2,
  input  [4:0] WriteReg,
  input  [31:0] WriteData,
  input  RegWrite,
  input  Clock,
  output [31:0] ReadData1,
  output [31:0] ReadData2
);

  wire _0, _1, _2, _3, _4, _5, _6, _7, _8, _9, _10, _11, _12, _13, _14, _15, _16, _17, _18, _19, _20, _21,
       _22, _23, _24, _25, _26, _27, _28, _29, _30, _31, and_1_out, and_2_out, and_3_out, and_4_out,
       and_5_out, and_6_out, and_7_out, and_8_out, and_9_out, and_10_out, and_11_out, and_12_out, and_13_out,
       and_14_out, and_15_out, and_16_out, and_17_out, and_18_out, and_19_out, and_20_out, and_21_out,
       and_22_out, and_23_out, and_24_out, and_25_out, and_26_out, and_27_out, and_28_out, and_29_out,
       and_30_out, and_31_out, and_32_out;
  wire [31:0] R0, R1, R2, R3, R4, R5, R6, R7, R8, R9, R10, R11, R12, R13, R14, R15, R16, R17, R18, R19, R20,
       R21, R22, R23, R24, R25, R26, R27, R28, R29, R30, R31;

  Register #(.Bits(32)) Register_0 (.D({32{1'b0}}), .C(Clock), .en(and_1_out), .Q(R0));
  and and_1 (and_1_out, _0, RegWrite);
  Register #(.Bits(32)) Register_1 (.D(WriteData), .C(Clock), .en(and_2_out), .Q(R1));
  and and_2 (and_2_out, _1, RegWrite);
  Register #(.Bits(32)) Register_2 (.D(WriteData), .C(Clock), .en(and_3_out), .Q(R2));
  and and_3 (and_3_out, _2, RegWrite);
  Register #(.Bits(32)) Register_3 (.D(WriteData), .C(Clock), .en(and_4_out), .Q(R3));
  and and_4 (and_4_out, _3, RegWrite);
  Register #(.Bits(32)) Register_4 (.D(WriteData), .C(Clock), .en(and_5_out), .Q(R4));
  and and_5 (and_5_out, _4, RegWrite);
  Register #(.Bits(32)) Register_5 (.D(WriteData), .C(Clock), .en(and_6_out), .Q(R5));
  and and_6 (and_6_out, _5, RegWrite);
  Register #(.Bits(32)) Register_6 (.D(WriteData), .C(Clock), .en(and_7_out), .Q(R6));
  and and_7 (and_7_out, _6, RegWrite);
  Register #(.Bits(32)) Register_7 (.D(WriteData), .C(Clock), .en(and_8_out), .Q(R7));
  Register #(.Bits(32)) Register_8 (.D(WriteData), .C(Clock), .en(and_9_out), .Q(R8));
  and and_8 (and_8_out, _7, RegWrite);
  and and_9 (and_9_out, _8, RegWrite);
  Register #(.Bits(32)) Register_9 (.D(WriteData), .C(Clock), .en(and_10_out), .Q(R9));
  and and_10 (and_10_out, _9, RegWrite);
  Register #(.Bits(32)) Register_10 (.D(WriteData), .C(Clock), .en(and_11_out), .Q(R10));
  and and_11 (and_11_out, _10, RegWrite);
  Register #(.Bits(32)) Register_11 (.D(WriteData), .C(Clock), .en(and_12_out), .Q(R11));
  Register #(.Bits(32)) Register_12 (.D(WriteData), .C(Clock), .en(and_13_out), .Q(R12));
  and and_12 (and_12_out, _11, RegWrite);
  and and_13 (and_13_out, _12, RegWrite);
  Register #(.Bits(32)) Register_13 (.D(WriteData), .C(Clock), .en(and_14_out), .Q(R13));
  and and_14 (and_14_out, _13, RegWrite);
  Register #(.Bits(32)) Register_14 (.D(WriteData), .C(Clock), .en(and_15_out), .Q(R14));
  and and_15 (and_15_out, _14, RegWrite);
  Multiplexer #(.Selector_Bits(5), .Bits(32)) multiplexer_1 (
    .sel(ReadReg1), .in_0(R0), .in_1(R1), .in_2(R2), .in_3(R3), .in_4(R4), .in_5(R5), .in_6(R6), .in_7(R7),
    .in_8(R8), .in_9(R9), .in_10(R10), .in_11(R11), .in_12(R12), .in_13(R13), .in_14(R14), .in_15(R15),
    .in_16(R16), .in_17(R17), .in_18(R18), .in_19(R19), .in_20(R20), .in_21(R21), .in_22(R22), .in_23(R23),
    .in_24(R24), .in_25(R25), .in_26(R26), .in_27(R27), .in_28(R28), .in_29(R29), .in_30(R30), .in_31(R31),
    .out(ReadData1));
  Register #(.Bits(32)) Register_15 (.D(WriteData), .C(Clock), .en(and_16_out), .Q(R15));
  and and_16 (and_16_out, _15, RegWrite);
  Register #(.Bits(32)) Register_16 (.D(WriteData), .C(Clock), .en(and_17_out), .Q(R16));
  and and_17 (and_17_out, _16, RegWrite);
  Register #(.Bits(32)) Register_17 (.D(WriteData), .C(Clock), .en(and_18_out), .Q(R17));
  and and_18 (and_18_out, _17, RegWrite);
  Register #(.Bits(32)) Register_18 (.D(WriteData), .C(Clock), .en(and_19_out), .Q(R18));
  and and_19 (and_19_out, _18, RegWrite);
  Multiplexer #(.Selector_Bits(5), .Bits(32)) multiplexer_2 (
    .sel(ReadReg2), .in_0(R0), .in_1(R1), .in_2(R2), .in_3(R3), .in_4(R4), .in_5(R5), .in_6(R6), .in_7(R7),
    .in_8(R8), .in_9(R9), .in_10(R10), .in_11(R11), .in_12(R12), .in_13(R13), .in_14(R14), .in_15(R15),
    .in_16(R16), .in_17(R17), .in_18(R18), .in_19(R19), .in_20(R20), .in_21(R21), .in_22(R22), .in_23(R23),
    .in_24(R24), .in_25(R25), .in_26(R26), .in_27(R27), .in_28(R28), .in_29(R29), .in_30(R30), .in_31(R31),
    .out(ReadData2));
  Register #(.Bits(32)) Register_19 (.D(WriteData), .C(Clock), .en(and_20_out), .Q(R19));
  Register #(.Bits(32)) Register_20 (.D(WriteData), .C(Clock), .en(and_21_out), .Q(R20));
  and and_20 (and_20_out, _19, RegWrite);
  Register #(.Bits(32)) Register_21 (.D(WriteData), .C(Clock), .en(and_22_out), .Q(R21));
  and and_21 (and_21_out, _20, RegWrite);
  Decoder #(.Selector_Bits(5)) decoder_1 (
    .sel(WriteReg), .out_0(_0), .out_1(_1), .out_2(_2), .out_3(_3), .out_4(_4), .out_5(_5), .out_6(_6),
    .out_7(_7), .out_8(_8), .out_9(_9), .out_10(_10), .out_11(_11), .out_12(_12), .out_13(_13), .out_14(_14),
    .out_15(_15), .out_16(_16), .out_17(_17), .out_18(_18), .out_19(_19), .out_20(_20), .out_21(_21),
    .out_22(_22), .out_23(_23), .out_24(_24), .out_25(_25), .out_26(_26), .out_27(_27), .out_28(_28),
    .out_29(_29), .out_30(_30), .out_31(_31));
  and and_22 (and_22_out, _21, RegWrite);
  Register #(.Bits(32)) Register_22 (.D(WriteData), .C(Clock), .en(and_23_out), .Q(R22));
  and and_23 (and_23_out, _22, RegWrite);
  Register #(.Bits(32)) Register_23 (.D(WriteData), .C(Clock), .en(and_24_out), .Q(R23));
  Register #(.Bits(32)) Register_24 (.D(WriteData), .C(Clock), .en(and_25_out), .Q(R24));
  and and_24 (and_24_out, _23, RegWrite);
  Register #(.Bits(32)) Register_25 (.D(WriteData), .C(Clock), .en(and_26_out), .Q(R25));
  and and_25 (and_25_out, _24, RegWrite);
  Register #(.Bits(32)) Register_26 (.D(WriteData), .C(Clock), .en(and_27_out), .Q(R26));
  and and_26 (and_26_out, _25, RegWrite);
  Register #(.Bits(32)) Register_27 (.D(WriteData), .C(Clock), .en(and_28_out), .Q(R27));
  and and_27 (and_27_out, _26, RegWrite);
  Register #(.Bits(32)) Register_28 (.D(WriteData), .C(Clock), .en(and_29_out), .Q(R28));
  Register #(.Bits(32)) Register_29 (.D(WriteData), .C(Clock), .en(and_30_out), .Q(R29));
  and and_28 (and_28_out, _27, RegWrite);
  Register #(.Bits(32)) Register_30 (.D(WriteData), .C(Clock), .en(and_31_out), .Q(R30));
  and and_29 (and_29_out, _28, RegWrite);
  Register #(.Bits(32)) Register_31 (.D(WriteData), .C(Clock), .en(and_32_out), .Q(R31));
  and and_30 (and_30_out, _29, RegWrite);
  and and_31 (and_31_out, _30, RegWrite);
  and and_32 (and_32_out, _31, RegWrite);

  // Other names for the same wires on the sheet: A[4:0] = WriteReg; B[31:0] = WriteData; RD1[31:0] = ReadData1;
  //   RD2[31:0] = ReadData2; RR1[4:0] = ReadReg1; RR2[4:0] = ReadReg2; RW = RegWrite
endmodule

/* Test case Register File Test:
WriteReg WriteData RegWrite Clock ReadReg1 ReadReg2 ReadData1 ReadData2

# $1 = 25
1 25 1 C 1 0 25 0

# $2 = 30
2 30 1 C 0 2 0 30

# $(N+1) = (N+1)
loop(N, 30)
	(N+1) (N+1) 1 C (N+1) (N) (N+1) (N)
end loop

# $(N+1) = N-60
loop(N, 30)
	(N+1) (N-60) 1 C (N+1) (N+1) (N-60) (N-60)
end loop

# Try writing to $0. This should not write anything
0 25 1 C 0 0 0 0

# try writing when RegWrite = 0
# (the registers should still have their old values)
loop(N, 30)
	(N+1) (N+80) 0 C (N+1) (N+1) (N-60) (N-60)
end loop
*/
