// Digital circuit add-sub.dig as structural Verilog
module add_sub (
  input  [31:0] B,
  input  [31:0] A,
  input  Sub,
  output [31:0] Out,
  output Overflow,
  output Sign
);

  wire and_1_out, and_2_out, and_3_out, and_4_out, not_2_out, not_3_out, not_4_out, not_5_out, not_6_out,
       not_7_out, or_1_out, or_2_out;
  wire [31:0] add_1_s, add_2_s, not_1_out;

  Add #(.Bits(32)) add_1 (.a(A), .b(B), .c_i(1'b0), .s(add_1_s));  // open: c_o
  assign not_1_out = ~B;  // Not not_1, 32 bits wide
  Add #(.Bits(32)) add_2 (.a(A), .b(not_1_out), .c_i(1'b1), .s(add_2_s));  // open: c_o
  not not_2 (not_2_out, Out[31]);
  not not_3 (not_3_out, A[31]);
  not not_4 (not_4_out, B[31]);
  not not_5 (not_5_out, B[31]);
  not not_6 (not_6_out, Out[31]);
  not not_7 (not_7_out, A[31]);
  and and_1 (and_1_out, A[31], B[31], not_2_out);
  and and_2 (and_2_out, A[31], not_5_out, not_6_out);
  and and_3 (and_3_out, not_3_out, not_4_out, Out[31]);
  and and_4 (and_4_out, not_7_out, B[31], Out[31]);
  or or_1 (or_1_out, and_1_out, and_3_out);
  or or_2 (or_2_out, and_2_out, and_4_out);
  Multiplexer #(.Bits(32)) multiplexer_1 (.sel(Sub), .in_0(add_1_s), .in_1(add_2_s), .out(Out));
  Multiplexer multiplexer_2 (.sel(Sub), .in_0(or_1_out), .in_1(or_2_out), .out(Overflow));

  assign Sign = Out[31];

  // Other names for the same wires on the sheet: R[31:0] = Out
endmodule

/* Test case Add-Sub Test:
A B Sub Out Overflow Sign
0x289322C4 0x01846399 0 0x2A17865D 0 0
0x4152A22D 0x22042121 0 0x6356C34E 0 0
0x84893212 0x0994AD1A 0 0x8E1DDF2C 0 1
0x90A8826C 0x112109FB 0 0xA1C98C67 0 1
0x5210C12D 0x3D04ABBC 0 0x8F156CE9 1 1
0x90D194B5 0xB005500E 0 0x40D6E4C3 1 0
0x39332544 0x0435FCAD 1 0x34FD2897 0 0
0x59286AB1 0x221FB76C 1 0x3708B345 0 0
0xECD55935 0x248C5A4B 1 0xC848FEEA 0 1
0x902A9525 0xE5454D48 1 0xAAE547DD 0 1
0x8211036A 0x7B13890A 1 0x06FD7A60 1 0
0x5FE15DBE 0x8934B9B1 1 0xD6ACA40D 1 1
*/
