// Digital circuit comparator.dig as structural Verilog
module comparator (
  input  Sign,
  input  Overflow,
  output Result
);

  wire and_1_out, and_2_out, not_1_out, not_2_out;

  not not_1 (not_1_out, Overflow);
  not not_2 (not_2_out, Sign);
  and and_1 (and_1_out, not_1_out, Sign);
  and and_2 (and_2_out, Overflow, not_2_out);
  or or_1 (Result, and_1_out, and_2_out);

  // Other names for the same wires on the sheet: o = Overflow; s = Sign
endmodule

/* Test case Comparator Test:
Sign Overflow Result
0 0 0
0 1 1
1 0 1
1 1 0
*/
