// Digital circuit control-unit.dig as structural Verilog
module control_unit (
  input  [6:0] opcode,
  input  [2:0] funct3,
  input  [6:0] funct7,
  output ALUOp0,
  output ALUOp1,
  output ALUOp2,
  output ALUOp3,
  output ImmSrc0,
  output ImmSrc1,
  output ALUSrc,
  output RegWrite
);

  wire ADDSUB, AND, I_TYPE, is_add, is_addi, is_and, is_andi, is_or, is_slt, is_slti, is_sub, OR, R_ADD,
       R_SUB, R_TYPE, SLT;
  wire [2:0] priorityencoder_1_num;

  and and_1 (is_add, R_TYPE, ADDSUB, R_ADD);
  and and_2 (is_sub, R_TYPE, ADDSUB, R_SUB);
  and and_3 (is_and, R_TYPE, AND, R_ADD);
  and and_4 (is_or, R_TYPE, OR, R_ADD);
  and and_5 (is_slt, R_TYPE, SLT, R_ADD);
  and and_6 (is_addi, I_TYPE, ADDSUB);
  and and_7 (is_slti, I_TYPE, SLT);
  and and_8 (is_andi, I_TYPE, AND);
  Comparator #(.Bits(7)) comparator_1 (.a(opcode), .b(7'b0110011), .eq(R_TYPE));  // open: gt, lt
  Comparator #(.Bits(7)) comparator_2 (.a(opcode), .b(7'b0010011), .eq(I_TYPE));  // open: gt, lt
  Comparator #(.Bits(3)) comparator_3 (.a(funct3), .b(3'b000), .eq(ADDSUB));  // open: gt, lt
  Comparator #(.Bits(3)) comparator_4 (.a(funct3), .b(3'b010), .eq(SLT));  // open: gt, lt
  Comparator #(.Bits(3)) comparator_5 (.a(funct3), .b(3'b110), .eq(OR));  // open: gt, lt
  Comparator #(.Bits(3)) comparator_6 (.a(funct3), .b(3'b111), .eq(AND));  // open: gt, lt
  Comparator #(.Bits(7)) comparator_7 (.a(funct7), .b({7{1'b0}}), .eq(R_ADD));  // open: gt, lt
  Comparator #(.Bits(7)) comparator_8 (.a(funct7), .b(7'b0100000), .eq(R_SUB));  // open: gt, lt
  PriorityEncoder #(.Selector_Bits(3)) priorityencoder_1 (
    .in0(is_add), .in1(is_sub), .in2(is_and), .in3(is_or), .in4(is_slt), .in5(is_addi), .in6(is_slti),
    .in7(is_andi), .num(priorityencoder_1_num));  // open: any
  ROM #(.AddrBits(3), .Bits(8)) rom_1 (
    .A(priorityencoder_1_num), .sel(1'b1),
    .D({RegWrite, ALUSrc, ImmSrc1, ImmSrc0, ALUOp3, ALUOp2, ALUOp1, ALUOp0}));

  // Notes on the sheet:
  //   contents of rom_1 (hex, n*v repeats v):
  //   82,86,80,81,87,c2,c7,c0
endmodule
