// Digital circuit cpu.dig as structural Verilog
module cpu (
  input  clk,
  output [31:0] ReadData1,
  output [31:0] ReadData2
);

  wire ALUSrc, ImmSrc0, ImmSrc1, RegWrite;
  wire [2:0] funct3;
  wire [3:0] ALUOp;
  wire [4:0] immediateRaw, rd, rs1;
  wire [6:0] funct7, opcode;
  wire [31:0] add_1_s, ALU_B, immediate, PC_q, ReadData2_Raw, Result;

  // alu alu_1: pin names not known; wires that end beside it: ReadData1, ALU_B, ALUOp, Result
  // Probe on ALU_B
  // Probe on Result
  // Probe on rd
  // Probe on rs1
  // Probe on funct3
  // Probe on immediateRaw
  // Probe on ReadData2
  // Probe on RegWrite
  // Probe on ReadData1
  Register #(.Bits(32), .isProgramCounter("true")) PC (.D(add_1_s), .C(clk), .en(1'b1), .Q(PC_q));
  register_file register_file_1 (
    .ReadReg1(rs1), .ReadReg2(immediateRaw), .WriteReg(rd), .WriteData(Result), .RegWrite(RegWrite),
    .Clock(clk), .ReadData1(ReadData1), .ReadData2(ReadData2_Raw));
  Add #(.Bits(32)) add_1 (.a(32'h4), .b(PC_q), .c_i(1'b0), .s(add_1_s));  // open: c_o
  // Probe on ALUOp
  // Probe on rs1
  // Probe on opcode
  // Probe on immediate
  // Probe on ReadData1
  // Probe on ALUSrc
  // Probe on ALUOp
  ROM #(.AddrBits(10), .isProgramMemory("true"), .Bits(32)) Instruction_Memory (
    .A(PC_q[11:2]), .sel(1'b1), .D({funct7, immediateRaw, rs1, funct3, rd, opcode}));
  control_unit control_unit_1 (
    .opcode(opcode), .funct3(funct3), .funct7(funct7), .ALUOp0(ALUOp[0]), .ALUOp1(ALUOp[1]),
    .ALUOp2(ALUOp[2]), .ALUOp3(ALUOp[3]), .ImmSrc0(ImmSrc0), .ImmSrc1(ImmSrc1), .ALUSrc(ALUSrc),
    .RegWrite(RegWrite));
  BitExtender #(.inputBits(12), .outputBits(32)) bitextender_1 (.in({funct7, immediateRaw}), .out(immediate));
  // Probe on opcode
  Multiplexer #(.Bits(32)) multiplexer_1 (.sel(ALUSrc), .in_0(ReadData2_Raw), .in_1({32{1'b0}}), .out(ReadData2));
  Multiplexer #(.Bits(32)) multiplexer_2 (.sel(ALUSrc), .in_0(ReadData2), .in_1(immediate), .out(ALU_B));

  // Other names for the same wires on the sheet: rs2[4:0] = immediateRaw; immediateRaw[11:5] = funct7; clock = clk

  // Notes on the sheet:
  //   contents of Instruction_Memory (hex, n*v repeats v):
  //   fec00213,7f020293,70128313,53130393,12337713,71c77793,5417f893
  //   ,13722913,292993,9aa13,ffda2a93,5aab13,b0013,fec22b93,b8013,fa65ac13
endmodule

/* Test case cpu:
clk ReadData1 ReadData2
0 0 0        # addi x4, x0, -20
C (-20) 0    # addi x5, x4, 0x7F0        ; x4 = -20
C 2012 0     # addi x6, x5, 0x701        ; x5 = 2012
C 3805 0     # addi x7, x6, 0x531        ; x6 = 3805

C 3805 0     # andi x14, x6, 0x123       ; x6 = 3805
C 1 0        # andi x15, x14, 0x71C      ; x14 = 1
C 0 0        # andi x17, x15, 0x541      ; x15 = 0

C (-20) 0    # slti x18, x4, 311         ; x4 = -20
C 1 0        # slti x19, x18, 2          ; x18 = 1
C 1 0        # slti x20, x19, 0          ; x19 = 1
C 0 0        # slti x21, x20, -3         ; x20 = 0
C 0 0        # slti x22, x21, 5          ; x21 = 0
C 1 0        # addi x0,  x22, 0          ; x22 = 1 (ignored write)

C (-20) 0    # slti x23, x4,  -20        ; x4 = -20
C 0 0        # addi x0,  x23, 0          ; x23 = 0

C 0 0        # slti x24, x11, -90        ; x11 = 0 (never written)
C 0 0        # addi x0,  x24, 0          ; x24 = 0

C (-20) 0    # slti x25, x4,  0          ; x4 = -20
C 1 0        # addi x0,  x25, 0          ; x25 = 1

C 0 0        # slti x26, x11, 600        ; x11 = 0
C 1 0        # addi x0,  x26, 0          ; x26 = 1

C (-20) 0    # slti x27, x4,  -1         ; x4 = -20
C 1 0        # addi x0,  x27, 0          ; x27 = 1
*/
