// Digital circuit register-file.dig as structural Verilog
module register_file (
  input  [4:0] ReadReg1,
  input  [4:0] ReadReg2,
  input  [4:0] WriteReg,
  input  [31:0] WriteData,
  input  RegWrite,
  input  Clock,
  output [31:0] ReadData1,
  output [31:0] ReadData2
);

  wire _0, _1, _1en, _2, _2en, _3, _3en, _4, _4en, _5, _5en, _6, _6en, _7, _7en, _8, _8en, _9, _9en, _10,
       _10en, _11, _11en, _12, _12en, _13, _13en, _14, _14en, _15, _15en, _16, _16en, _17, _17en, _18, _18en,
       _19, _19en, _20, _20en, _21, _21en, _22, _22en, _23, _23en, _24, _24en, _25, _25en, _26, _26en, _27,
       _27en, _28, _28en, _29, _29en, _30, _30en, _31, _31en;
  wire [31:0] Q0, Q1, Q2, Q3, Q4, Q5, Q6, Q7, Q8, Q9, Q10, Q11, Q12, Q13, Q14, Q15, Q16, Q17, Q18, Q19, Q20,
       Q21, Q22, Q23, Q24, Q25, Q26, Q27, Q28, Q29, Q30, Q31;

  Decoder #(.Selector_Bits(5)) decoder_1 (
    .sel(WriteReg), .out_0(_0), .out_1(_1), .out_2(_2), .out_3(_3), .out_4(_4), .out_5(_5), .out_6(_6),
    .out_7(_7), .out_8(_8), .out_9(_9), .out_10(_10), .out_11(_11), .out_12(_12), .out_13(_13), .out_14(_14),
    .out_15(_15), .out_16(_16), .out_17(_17), .out_18(_18), .out_19(_19), .out_20(_20), .out_21(_21),
    .out_22(_22), .out_23(_23), .out_24(_24), .out_25(_25), .out_26(_26), .out_27(_27), .out_28(_28),
    .out_29(_29), .out_30(_30), .out_31(_31));
  and and_1 (_1en, _1, RegWrite);
  and and_2 (_2en, _2, RegWrite);
  and and_3 (_3en, _3, RegWrite);
  and and_4 (_4en, _4, RegWrite);
  and and_5 (_5en, _5, RegWrite);
  and and_6 (_6en, _6, RegWrite);
  and and_7 (_7en, _7, RegWrite);
  and and_8 (_8en, _8, RegWrite);
  and and_9 (_9en, _9, RegWrite);
  and and_10 (_10en, _10, RegWrite);
  and and_11 (_11en, _11, RegWrite);
  and and_12 (_12en, _12, RegWrite);
  and and_13 (_13en, _13, RegWrite);
  and and_14 (_14en, _14, RegWrite);
  and and_15 (_15en, _15, RegWrite);
  and and_16 (_16en, _16, RegWrite);
  and and_17 (_17en, _17, RegWrite);
  and and_18 (_18en, _18, RegWrite);
  and and_19 (_19en, _19, RegWrite);
  and and_20 (_20en, _20, RegWrite);
  and and_21 (_21en, _21, RegWrite);
  and and_22 (_22en, _22, RegWrite);
  and and_23 (_23en, _23, RegWrite);
  and and_24 (_24en, _24, RegWrite);
  and and_25 (_25en, _25, RegWrite);
  and and_26 (_26en, _26, RegWrite);
  and and_27 (_27en, _27, RegWrite);
  and and_28 (_28en, _28, RegWrite);
  and and_29 (_29en, _29, RegWrite);
  and and_30 (_30en, _30, RegWrite);
  and and_31 (_31en, _31, RegWrite);
  Register #(.Bits(32)) Reg0 (.D({32{1'b0}}), .C(Clock), .en(1'b0), .Q(Q0));
  Register #(.Bits(32)) Reg1 (.D(WriteData), .C(Clock), .en(_1en), .Q(Q1));
  Register #(.Bits(32)) Reg2 (.D(WriteData), .C(Clock), .en(_2en), .Q(Q2));
  Register #(.Bits(32)) Reg3 (.D(WriteData), .C(Clock), .en(_3en), .Q(Q3));
  Register #(.Bits(32)) Reg4 (.D(WriteData), .C(Clock), .en(_4en), .Q(Q4));
  Register #(.Bits(32)) Reg5 (.D(WriteData), .C(Clock), .en(_5en), .Q(Q5));
  Register #(.Bits(32)) Reg6 (.D(WriteData), .C(Clock), .en(_6en), .Q(Q6));
  Register #(.Bits(32)) Reg7 (.D(WriteData), .C(Clock), .en(_7en), .Q(Q7));
  Register #(.Bits(32)) Reg8 (.D(WriteData), .C(Clock), .en(_8en), .Q(Q8));
  Register #(.Bits(32)) Reg9 (.D(WriteData), .C(Clock), .en(_9en), .Q(Q9));
  Register #(.Bits(32)) Reg10 (.D(WriteData), .C(Clock), .en(_10en), .Q(Q10));
  Register #(.Bits(32)) Reg11 (.D(WriteData), .C(Clock), .en(_11en), .Q(Q11));
  Register #(.Bits(32)) Reg12 (.D(WriteData), .C(Clock), .en(_12en), .Q(Q12));
  Register #(.Bits(32)) Reg13 (.D(WriteData), .C(Clock), .en(_13en), .Q(Q13));
  Register #(.Bits(32)) Reg14 (.D(WriteData), .C(Clock), .en(_14en), .Q(Q14));
  Register #(.Bits(32)) Reg15 (.D(WriteData), .C(Clock), .en(_15en), .Q(Q15));
  Register #(.Bits(32)) Reg16 (.D(WriteData), .C(Clock), .en(_16en), .Q(Q16));
  Register #(.Bits(32)) Reg17 (.D(WriteData), .C(Clock), .en(_17en), .Q(Q17));
  Register #(.Bits(32)) Reg18 (.D(WriteData), .C(Clock), .en(_18en), .Q(Q18));
  Register #(.Bits(32)) Reg19 (.D(WriteData), .C(Clock), .en(_19en), .Q(Q19));
  Register #(.Bits(32)) Reg20 (.D(WriteData), .C(Clock), .en(_20en), .Q(Q20));
  Register #(.Bits(32)) Reg21 (.D(WriteData), .C(Clock), .en(_21en), .Q(Q21));
  Register #(.Bits(32)) Reg22 (.D(WriteData), .C(Clock), .en(_22en), .Q(Q22));
  Register #(.Bits(32)) Reg23 (.D(WriteData), .C(Clock), .en(_23en), .Q(Q23));
  Register #(.Bits(32)) Reg24 (.D(WriteData), .C(Clock), .en(_24en), .Q(Q24));
  Register #(.Bits(32)) Reg25 (.D(WriteData), .C(Clock), .en(_25en), .Q(Q25));
  Register #(.Bits(32)) Reg26 (.D(WriteData), .C(Clock), .en(_26en), .Q(Q26));
  Register #(.Bits(32)) Reg27 (.D(WriteData), .C(Clock), .en(_27en), .Q(Q27));
  Register #(.Bits(32)) Reg28 (.D(WriteData), .C(Clock), .en(_28en), .Q(Q28));
  Register #(.Bits(32)) Reg29 (.D(WriteData), .C(Clock), .en(_29en), .Q(Q29));
  Register #(.Bits(32)) Reg30 (.D(WriteData), .C(Clock), .en(_30en), .Q(Q30));
  Register #(.Bits(32)) Reg31 (.D(WriteData), .C(Clock), .en(_31en), .Q(Q31));
  Multiplexer #(.Selector_Bits(5), .Bits(32)) multiplexer_1 (
    .sel(ReadReg1), .in_0(Q0), .in_1(Q1), .in_2(Q2), .in_3(Q3), .in_4(Q4), .in_5(Q5), .in_6(Q6), .in_7(Q7),
    .in_8(Q8), .in_9(Q9), .in_10(Q10), .in_11(Q11), .in_12(Q12), .in_13(Q13), .in_14(Q14), .in_15(Q15),
    .in_16(Q16), .in_17(Q17), .in_18(Q18), .in_19(Q19), .in_20(Q20), .in_21(Q21), .in_22(Q22), .in_23(Q23),
    .in_24(Q24), .in_25(Q25), .in_26(Q26), .in_27(Q27), .in_28(Q28), .in_29(Q29), .in_30(Q30), .in_31(Q31),
    .out(ReadData1));
  Multiplexer #(.Selector_Bits(5), .Bits(32)) multiplexer_2 (
    .sel(ReadReg2), .in_0(Q0), .in_1(Q1), .in_2(Q2), .in_3(Q3), .in_4(Q4), .in_5(Q5), .in_6(Q6), .in_7(Q7),
    .in_8(Q8), .in_9(Q9), .in_10(Q10), .in_11(Q11), .in_12(Q12), .in_13(Q13), .in_14(Q14), .in_15(Q15),
    .in_16(Q16), .in_17(Q17), .in_18(Q18), .in_19(Q19), .in_20(Q20), .in_21(Q21), .in_22(Q22), .in_23(Q23),
    .in_24(Q24), .in_25(Q25), .in_26(Q26), .in_27(Q27), .in_28(Q28), .in_29(Q29), .in_30(Q30), .in_31(Q31),
    .out(ReadData2));

  // Other names for the same wires on the sheet: C = Clock; RD1[31:0] = ReadData1; RD2[31:0] = ReadData2;
  //   RR1[4:0] = ReadReg1; RR2[4:0] = ReadReg2; RW = RegWrite; WD[31:0] = WriteData; WR[4:0] = WriteReg
endmodule

/* Test case Register File Test:
WriteReg WriteData RegWrite Clock ReadReg1 ReadReg2 ReadData1 ReadData2

# $1 = 25
1 25 1 C 1 0 25 0

# $2 = 30
2 30 1 C 0 2 0 30

# $(N+1) = (N+1)
loop(N, 30)
	(N+1) (N+1) 1 C (N+1) (N) (N+1) (N)
end loop

# $(N+1) = N-60
loop(N, 30)
	(N+1) (N-60) 1 C (N+1) (N+1) (N-60) (N-60)
end loop

# Try writing to $0. This should not write anything
0 25 1 C 0 0 0 0

# try writing when RegWrite = 0
# (the registers should still have their old values)
loop(N, 30)
	(N+1) (N+80) 0 C (N+1) (N+1) (N-60) (N-60)
end loop
*/
